# Fritzing sketch Untitled Sketch 2 (saved by Fritzing 0.9.3b)
breadboards: 1

parts:
  IC1 = L293D [package=THT]
  VCC1 = 4 x AAA Battery Mount
  Part1 = Arduino Uno (Rev3) - ICSP
  M2 = DC Motor
  HC-SR04_Sensor_1 = HC-SR04 Ultrasonic Distance Sensor
  HC-SR04_Sensor_2 = HC-SR04 Ultrasonic Distance Sensor
  HC-SR04_Sensor_3 = HC-SR04 Ultrasonic Distance Sensor
  M3 = DC Motor
  IR1 = TSOP312.., 314.. [package=THT]
  LED1 = smd LED [color="Green (560nm)" package="0805 [SMD]"]
  LED2 = smd LED [color="Blue (430nm)" package="0805 [SMD]"]
  R1 = Resistor [tolerance=±5% resistance=220 package="2010 [SMD]"]
  R2 = Resistor [tolerance=±5% resistance=220 package="2010 [SMD]"]
  VCC2 = Battery block 9V  # not connected

nets:
  N1: IC1.Enable_1, Part1.D5_PWM
  GND: IC1.0V, VCC1.-, Part1.GND, HC-SR04_Sensor_1.GND, HC-SR04_Sensor_2.GND, HC-SR04_Sensor_3.GND, IR1.Vs, LED1.anode, R1.Pin_1
  N2: IC1.+Vmotor, VCC1.+
  N3: IC1.Enable_2, Part1.D6_PWM
  VCC: IC1.+V, Part1.5V, HC-SR04_Sensor_1.VCC, HC-SR04_Sensor_2.VCC, HC-SR04_Sensor_3.VCC, IR1.Data
  N4: Part1.A0, HC-SR04_Sensor_2.ECHO
  N5: Part1.A1, HC-SR04_Sensor_1.ECHO
  N6: Part1.A2, IR1.GND
  N7: Part1.A3, HC-SR04_Sensor_3.ECHO
  N8: Part1.A4/SDA, R2.Pin_1
  N9: Part1.D8, M2.pin_1
  N10: Part1.D9_PWM, HC-SR04_Sensor_3.TRIG
  N11: Part1.D10_PWM/SS, HC-SR04_Sensor_2.TRIG
  N12: Part1.D11_PWM/MOSI, HC-SR04_Sensor_1.TRIG
  N13: Part1.D12/MISO, LED2.cathode
  N14: Part1.D3_PWM, M3.pin_2
  N15: Part1.D4, M3.pin_1
  N16: Part1.D7, M2.pin_2
